// Logisim project project3.circ as structural Verilog: 1 circuit, main circuit main
module main (
  input  States,
  output R1,
  output Y1,
  output G1,
  output R2,
  output Y2,
  output G2
);

  wire and_1_out, and_2_out, and_3_out, clock_1_out, d_ff_1_qn, d_ff_2_qn, d_ff_3_q, d_ff_3_qn, not_1_out,
       or_1_out, or_2_out, or_3_out;

  Clock clock_1 (.out(clock_1_out));
  not not_1 (not_1_out, States);
  and and_1 (and_1_out, not_1_out, d_ff_2_qn);
  and and_2 (and_2_out, d_ff_1_qn, not_1_out);
  and and_3 (and_3_out, R1, d_ff_3_q);
  or or_1 (or_1_out, and_1_out, d_ff_3_qn);
  or or_2 (or_2_out, and_2_out, d_ff_3_q);
  or or_3 (or_3_out, and_3_out, d_ff_2_qn);
  D_Flip_Flop d_ff_1 (.D(or_1_out), .clk(clock_1_out), .Q(R1), .Qn(d_ff_1_qn));  // open: preset, reset
  D_Flip_Flop d_ff_2 (.D(or_2_out), .clk(clock_1_out), .Q(R2), .Qn(d_ff_2_qn));  // open: preset, reset
  D_Flip_Flop d_ff_3 (.D(or_3_out), .clk(clock_1_out), .Q(d_ff_3_q), .Qn(d_ff_3_qn));  // open: preset, reset
  and and_4 (Y1, d_ff_1_qn, d_ff_3_qn);
  and and_5 (Y2, d_ff_2_qn, d_ff_3_q);
  and and_6 (G1, d_ff_1_qn, d_ff_3_q);
  and and_7 (G2, d_ff_2_qn, d_ff_3_qn);
endmodule
